# Fritzing sketch P07_00_00-CalibrateSensors (saved by Fritzing 0.9.3b)
breadboards: 1

parts:
  Part1 = Arduino Pro Mini v13
  J3 = female pin header, 7 pins [form="♀ (female)"]
  R1 = Resistor [tolerance=±5% resistance=100 package=THT]
  R2 = Resistor [tolerance=±5% resistance=100 package=THT]
  R3 = Resistor [tolerance=±5% resistance=100 package=THT]
  R4 = Resistor [tolerance=±5% resistance=220 package=THT]
  R5 = Resistor [tolerance=±5% resistance=220 package=THT]
  R6 = Resistor [tolerance=±5% resistance=220 package=THT]
  S4 = female pin header, 2 pins [form="♀ (female)"]
  R19 = Resistor [tolerance=±5% resistance=10k package=THT]
  S1 = female pin header, 2 pins [form="♀ (female)"]
  S2 = female pin header, 2 pins [form="♀ (female)"]
  S3 = female pin header, 2 pins [form="♀ (female)"]
  R20 = Resistor [tolerance=±5% resistance=10k package=THT]
  R21 = Resistor [tolerance=±5% resistance=10k package=THT]
  R22 = Resistor [tolerance=±5% resistance=10k package=THT]

nets:
  N1: Part1.GND, J3.pin5, R4.Pin_1, R5.Pin_1, R6.Pin_1, R19.Pin_0, R20.Pin_0, R21.Pin_0, R22.Pin_0
  N2: Part1.VCC, J3.pin4
  N3: Part1.A3, S4.pin1, R19.Pin_1
  N4: Part1.A2, S3.pin1, R20.Pin_1
  N5: Part1.A1, S2.pin1, R21.Pin_1
  N6: Part1.A0, S1.pin1, R22.Pin_1
  N7: Part1.D13/SCK, R3.Pin_0
  N8: Part1.D12/MISO, J3.pin3
  N9: Part1.D11_PWM/MOSI, R2.Pin_0
  N10: Part1.D10_PWM/SS, R1.Pin_0
  N11: Part1.D6_PWM, S1.pin2
  N12: Part1.D5_PWM, S2.pin2
  N13: Part1.D4, S3.pin2
  N14: Part1.D3_PWM, S4.pin2
  N15: J3.pin1, R3.Pin_1, R4.Pin_0
  N16: J3.pin6, R2.Pin_1, R5.Pin_0
  N17: J3.pin7, R1.Pin_1, R6.Pin_0
