# Fritzing sketch P07_00_00-Main (saved by Fritzing 0.9.3b)
breadboards: 1

parts:
  Part1 = Arduino Pro Mini v13
  J3 = female pin header, 7 pins [form="♀ (female)"]
  R1 = Resistor [tolerance=±5% resistance=100 package=THT]
  R2 = Resistor [tolerance=±5% resistance=100 package=THT]
  R3 = Resistor [tolerance=±5% resistance=100 package=THT]
  R4 = Resistor [tolerance=±5% resistance=220 package=THT]
  R5 = Resistor [tolerance=±5% resistance=220 package=THT]
  R6 = Resistor [tolerance=±5% resistance=220 package=THT]
  Q1 = PNP-Transistor [package="TO92 [THT]"]
  Q2 = PNP-Transistor [package="TO92 [THT]"]
  Q3 = PNP-Transistor [package="TO92 [THT]"]
  R10 = Resistor [tolerance=±5% resistance=270 package=THT]
  R11 = Resistor [tolerance=±5% resistance=270 package=THT]
  R12 = Resistor [tolerance=±5% resistance=270 package=THT]
  Motor03 = DC Motor
  D1 = Rectifier Diode [part_number=1N4001 package="300 mil [THT]"]
  Motor02 = DC Motor
  D2 = Rectifier Diode [part_number=1N4001 package="300 mil [THT]"]
  Motor01 = DC Motor
  D3 = Rectifier Diode [part_number=1N4001 package="300 mil [THT]"]
  S4 = female pin header, 2 pins [form="♀ (female)"]
  R19 = Resistor [tolerance=±5% resistance=10k package=THT]
  S1 = female pin header, 2 pins [form="♀ (female)"]
  S2 = female pin header, 2 pins [form="♀ (female)"]
  S3 = female pin header, 2 pins [form="♀ (female)"]
  R20 = Resistor [tolerance=±5% resistance=10k package=THT]
  R21 = Resistor [tolerance=±5% resistance=10k package=THT]
  R22 = Resistor [tolerance=±5% resistance=10k package=THT]

nets:
  N1: Part1.RAW, Motor03.pin_2, D1.anode, Motor02.pin_2, D2.anode, Motor01.pin_2, D3.anode
  N2: Part1.GND, J3.pin5, R4.Pin_1, R5.Pin_1, R6.Pin_1, Q1.E, Q2.E, Q3.E, R19.Pin_0, R20.Pin_0, R21.Pin_0, R22.Pin_0
  N3: Part1.VCC, J3.pin4
  N4: Part1.A3, S4.pin1, R19.Pin_1
  N5: Part1.A2, S3.pin1, R20.Pin_1
  N6: Part1.A1, S2.pin1, R21.Pin_1
  N7: Part1.A0, S1.pin1, R22.Pin_1
  N8: Part1.D13/SCK, R3.Pin_0
  N9: Part1.D12/MISO, J3.pin3
  N10: Part1.D11_PWM/MOSI, R2.Pin_0
  N11: Part1.D10_PWM/SS, R1.Pin_0
  N12: Part1.D9_PWM, R10.Pin_1
  N13: Part1.D8, R11.Pin_1
  N14: Part1.D7, R12.Pin_1
  N15: Part1.D6_PWM, S1.pin2
  N16: Part1.D5_PWM, S2.pin2
  N17: Part1.D4, S3.pin2
  N18: Part1.D3_PWM, S4.pin2
  N19: J3.pin1, R3.Pin_1, R4.Pin_0
  N20: J3.pin6, R2.Pin_1, R5.Pin_0
  N21: J3.pin7, R1.Pin_1, R6.Pin_0
  N22: Q1.B, R10.Pin_0
  N23: Q1.C, Motor01.pin_1, D3.cathode
  N24: Q2.B, R11.Pin_0
  N25: Q2.C, Motor02.pin_1, D2.cathode
  N26: Q3.B, R12.Pin_0
  N27: Q3.C, Motor03.pin_1, D1.cathode
