# Fritzing sketch P07_00_00-TestSD (saved by Fritzing 0.9.3b)
breadboards: 1

parts:
  Part1 = Arduino Pro Mini v13
  J4 = female pin header, 7 pins [form="♀ (female)"]
  R7 = Resistor [tolerance=±5% resistance=100 package=THT]
  R8 = Resistor [tolerance=±5% resistance=100 package=THT]
  R9 = Resistor [tolerance=±5% resistance=100 package=THT]
  R10 = Resistor [tolerance=±5% resistance=220 package=THT]
  R11 = Resistor [tolerance=±5% resistance=220 package=THT]
  R12 = Resistor [tolerance=±5% resistance=220 package=THT]

nets:
  N1: Part1.GND, J4.pin5, R10.Pin_1, R11.Pin_1, R12.Pin_1
  N2: Part1.VCC, J4.pin4
  N3: Part1.D13/SCK, R7.Pin_0
  N4: Part1.D12/MISO, J4.pin3
  N5: Part1.D11_PWM/MOSI, R8.Pin_0
  N6: Part1.D10_PWM/SS, R9.Pin_0
  N7: J4.pin1, R7.Pin_1, R12.Pin_0
  N8: J4.pin6, R8.Pin_1, R11.Pin_0
  N9: J4.pin7, R9.Pin_1, R10.Pin_0
