# Fritzing sketch P07_00_00-TestSensor (saved by Fritzing 0.9.3b)
breadboards: 1

parts:
  Part1 = Arduino Pro Mini v13
  Part2 = Soil Moisture Sensor
  R23 = Resistor [tolerance=±5% resistance=10k package=THT]
  Soil_Moisture_Sensor = female pin header, 2 pins [form="♀ (female)"]

nets:
  N1: Part1.GND, R23.Pin_0
  N2: Part1.A0, Part2.VCC, R23.Pin_1, Soil_Moisture_Sensor.pin1
  N3: Part1.D6_PWM, Part2.SIG, Soil_Moisture_Sensor.pin2
